# Fritzing sketch SOE - v1 (saved by Fritzing 0.9.5d)
breadboards: 1

parts:
  Raspberry_Pi_1 = Raspberry Pi 3 [part_number=RPI-3-V1.2]
  BC548 = NPN-Transistor [package="TO92 [THT]"]
  R3 = Resistor [tolerance=±5% resistance=330 package="2010 [SMD]"]
  TIP31C = npn-Powertransistor [package="TO220 [THT]"]
  1N4007 = Rectifier Diode [part_number=1N4001 package="300 mil [THT]"]
  C1 = Electrolytic Capacitor [capacitance=0.47mF voltage=20V package="200 mil [THT, electrolytic]"]
  LED1 = RGB LED (com. anode, rbg) [package="5 mm [THT]"]
  R2 = Resistor [tolerance=±5% resistance=330 package="2010 [SMD]"]
  R1 = Resistor [tolerance=±5% resistance=330 package="2010 [SMD]"]
  R4 = Resistor [tolerance=±5% resistance=10k package="2010 [SMD]"]
  R5 = Resistor [tolerance=±5% resistance=330 package="2010 [SMD]"]
  L1 = Solenoid

nets:
  N1: Raspberry_Pi_1.GPIO17, R1.Pin_1
  N2: Raspberry_Pi_1.GPIO27, R5.Pin_1
  N3: Raspberry_Pi_1.GPIO22, R2.Pin_0
  N4: Raspberry_Pi_1.GPIO10, R3.Pin_1
  N5: Raspberry_Pi_1.GND, Raspberry_Pi_1.GPIO14, TIP31C.emitter, C1.-, LED1.common_anode, R4.Pin_1
  N6: Raspberry_Pi_1.5V, BC548.E, C1.+
  N7: BC548.B, TIP31C.base
  N8: BC548.C, R1.Pin_0, R4.Pin_0
  N9: R3.Pin_0, LED1.green_cathode
  N10: TIP31C.collector, 1N4007.anode, L1.pin1
  N11: 1N4007.cathode, L1.pin2
  N12: LED1.red_cathode, R2.Pin_1
  N13: LED1.blue_cathode, R5.Pin_0
